// Logisim project scheme.circ as structural Verilog
module Arithmetic_Logic_Unit (
  input  C,
  input  R,
  input  EZ,
  input  i,
  input  EF,
  input  LX,
  input  LY,
  input  [7:0] D,
  input  [7:0] OP,
  output [7:0] S
);

  wire Adc___Sbb_co, and_1_out, and_2_out, and_3_out, and_4_out, and_5_out, and_6_out, and_7_out, or_2_out,
       or_3_out, Right_Shift_o;
  wire [3:0] or_1_out;
  wire [7:0] Adc___Sbb_s, Bitwise_AND_and, Bitwise_NOR_nor, Bitwise_OR_or, Decoder_d, Reg_X_q, Reg_Y_q,
       Right_Shift_sft;

  and and_1 (and_1_out, C, LX);
  and and_2 (and_2_out, LY, C);
  and and_3 (and_3_out, OP[4], OP[6]);
  D_Latch Reg_X (.D(D), .R(R), .E(and_1_out), .Q(Reg_X_q));
  D_Latch Reg_Y (.D(D), .R(R), .E(and_2_out), .Q(Reg_Y_q));
  and and_4 (and_4_out, and_3_out, ~OP[5]);  // AND_Gate
  and and_5 (and_5_out, OP[5], OP[6]);
  // Probe on Reg_X_q
  // Probe on Reg_Y_q
  Decoder Decoder (.C(OP[6:4]), .E(EZ), .D(Decoder_d));
  BitAnd Bitwise_AND (.A(Reg_X_q), .B(Reg_Y_q), .AND(Bitwise_AND_and));
  BitOr Bitwise_OR (.A(Reg_X_q), .B(Reg_Y_q), .OR(Bitwise_OR_or));
  BitNor Bitwise_NOR (.A(Reg_X_q), .B(Reg_Y_q), .NOR(Bitwise_NOR_nor));
  RightShift Right_Shift (.A(Reg_X_q), .i(i), .o(Right_Shift_o), .SFT(Right_Shift_sft));
  AdcSbb Adc___Sbb (.A_S(Decoder_d[7]), .Ci(i), .A(Reg_X_q), .B(Reg_Y_q), .S(Adc___Sbb_s), .Co(Adc___Sbb_co));
  Comparator Comparator (.A(Reg_X_q), .B(Reg_Y_q), .A_B(or_1_out[1]), .A_B_2(or_1_out[2]), .A_B_3(or_1_out[3]));
  and and_6 (and_6_out, Right_Shift_o, and_4_out);
  or or_1 (or_1_out[0], and_6_out, and_7_out);
  and and_7 (and_7_out, Adc___Sbb_co, and_5_out);
  or or_2 (or_2_out, EF, Decoder_d[1]);
  assign S = Decoder_d[2] ? Bitwise_AND_and : 8'bz;  // Controlled_Buffer controlled_buffer_1
  assign S = Decoder_d[3] ? Bitwise_OR_or : 8'bz;  // Controlled_Buffer controlled_buffer_2
  assign S = Decoder_d[4] ? Bitwise_NOR_nor : 8'bz;  // Controlled_Buffer controlled_buffer_3
  assign S = Decoder_d[5] ? Right_Shift_sft : 8'bz;  // Controlled_Buffer controlled_buffer_4
  or or_3 (or_3_out, Decoder_d[6], Decoder_d[7]);
  assign S = or_3_out ? Adc___Sbb_s : 8'bz;  // Controlled_Buffer controlled_buffer_5
  assign S = or_2_out ? {4'b0000, or_1_out} : 8'bz;  // Controlled_Buffer controlled_buffer_6
endmodule

module General_Purpose_Registers (
  input  LF,
  input  LG,
  input  [7:0] D,
  input  LH,
  input  R,
  input  [7:0] OP,
  input  C,
  input  LR,
  input  ER,
  input  EA,
  output [7:0] Q,
  output i,
  output [15:0] A
);

  wire and_1_out, and_2_out, and_3_out, and_4_out, or_1_out, or_2_out, or_3_out;
  wire [7:0] Input_d, Output_d, Reg_A_q, Reg_B_q, Reg_C_q, Reg_D_q, Reg_E_q, Reg_G_q, Reg_H_q;
  wire [7:1] Reg_F_q;

  Decoder Input (.C(OP[2:0]), .E(and_1_out), .D(Input_d));
  and and_1 (and_1_out, C, LR);
  Decoder Output (.C(OP[2:0]), .E(ER), .D(Output_d));
  D_Latch Reg_A (.D(D), .R(R), .E(Input_d[0]), .Q(Reg_A_q));
  assign Q = Output_d[0] ? Reg_A_q : 8'bz;  // Controlled_Buffer controlled_buffer_1
  assign Q = Output_d[1] ? Reg_B_q : 8'bz;  // Controlled_Buffer controlled_buffer_2
  D_Latch Reg_B (.D(D), .R(R), .E(Input_d[1]), .Q(Reg_B_q));
  assign Q = Output_d[2] ? Reg_C_q : 8'bz;  // Controlled_Buffer controlled_buffer_3
  D_Latch Reg_C (.D(D), .R(R), .E(Input_d[2]), .Q(Reg_C_q));
  D_Latch Reg_D (.D(D), .R(R), .E(Input_d[3]), .Q(Reg_D_q));
  assign Q = Output_d[3] ? Reg_D_q : 8'bz;  // Controlled_Buffer controlled_buffer_4
  and and_2 (and_2_out, C, LF);
  and and_3 (and_3_out, C, LG);
  and and_4 (and_4_out, C, LH);
  or or_1 (or_1_out, and_2_out, Input_d[5]);
  or or_2 (or_2_out, and_3_out, Input_d[6]);
  or or_3 (or_3_out, and_4_out, Input_d[7]);
  D_Latch Reg_E (.D(D), .R(R), .E(Input_d[4]), .Q(Reg_E_q));
  D_Latch Reg_F (.D(D), .R(R), .E(or_1_out), .Q({Reg_F_q, i}));
  D_Latch Reg_G (.D(D), .R(R), .E(or_2_out), .Q(Reg_G_q));
  D_Latch Reg_H (.D(D), .R(R), .E(or_3_out), .Q(Reg_H_q));
  assign Q = Output_d[4] ? Reg_E_q : 8'bz;  // Controlled_Buffer controlled_buffer_5
  assign Q = Output_d[5] ? {Reg_F_q, i} : 8'bz;  // Controlled_Buffer controlled_buffer_6
  assign Q = Output_d[6] ? Reg_G_q : 8'bz;  // Controlled_Buffer controlled_buffer_7
  assign Q = Output_d[7] ? Reg_H_q : 8'bz;  // Controlled_Buffer controlled_buffer_8
  assign A = EA ? {Reg_H_q, Reg_G_q} : 16'bz;  // Controlled_Buffer controlled_buffer_9
endmodule
